// Logisim project Parte_c.circ as structural Verilog
module A (
  input  N0,
  input  N1,
  input  N2,
  input  N3,
  output f_a
);

  wire or_1_out, or_2_out, or_3_out, or_4_out;

  or or_1 (or_1_out, N3, N2, N1, ~N0);  // OR_Gate
  or or_2 (or_2_out, N3, ~N2, N1, N0);  // OR_Gate
  or or_3 (or_3_out, ~N3, N2, ~N1, ~N0);  // OR_Gate
  or or_4 (or_4_out, ~N3, ~N2, N1, ~N0);  // OR_Gate
  and and_1 (f_a, or_1_out, or_2_out, or_3_out, or_4_out);
endmodule

module Display_7seg (
  input  N3,
  input  N2,
  input  N1,
  input  N0
);

  wire a_1_f_a, b_1_f_b, c_1_f_c, d_1_f_d, e_1_f_e, f_1_f_f, g_1_f_g;

  E e_1 (.N0(N0), .N1(N1), .N2(N2), .N3(N3), .f_e(e_1_f_e));
  F f_1 (.N0(N0), .N1(N1), .N2(N2), .N3(N3), .f_f(f_1_f_f));
  G g_1 (.N0(N0), .N1(N1), .N2(N2), .N3(N3), .f_g(g_1_f_g));
  _7_Segment_Display u_7_segment_display_1 (
    .g(g_1_f_g), .f(f_1_f_f), .a(a_1_f_a), .b(b_1_f_b), .e(e_1_f_e), .d(d_1_f_d), .c(c_1_f_c));  // open: dp
  D d_1 (.N0(N0), .N1(N1), .N2(N2), .N3(N3), .f_d(d_1_f_d));
  A a_1 (.N0(N0), .N1(N1), .N2(N2), .N3(N3), .f_a(a_1_f_a));
  C c_1 (.N0(N0), .N1(N1), .N2(N2), .N3(N3), .f_c(c_1_f_c));
  B b_1 (.N0(N0), .N1(N1), .N2(N2), .N3(N3), .f_b(b_1_f_b));
endmodule

module B (
  input  N0,
  input  N1,
  input  N2,
  input  N3,
  output f_b
);

  wire or_1_out, or_2_out, or_3_out, or_4_out, or_5_out, or_6_out;

  or or_1 (or_1_out, N3, ~N2, N1, ~N0);  // OR_Gate
  or or_2 (or_2_out, N3, ~N2, ~N1, N0);  // OR_Gate
  or or_3 (or_3_out, ~N3, N2, ~N1, ~N0);  // OR_Gate
  or or_4 (or_4_out, ~N3, ~N2, N1, N0);  // OR_Gate
  or or_5 (or_5_out, ~N3, ~N2, ~N1, N0);  // OR_Gate
  or or_6 (or_6_out, ~N3, ~N2, ~N1, ~N0);  // OR_Gate
  and and_1 (f_b, or_1_out, or_2_out, or_3_out, or_4_out, or_5_out, or_6_out);
endmodule

module C (
  input  N0,
  input  N1,
  input  N2,
  input  N3,
  output f_c
);

  wire or_1_out, or_2_out, or_3_out, or_4_out;

  or or_1 (or_1_out, N3, N2, ~N1, N0);  // OR_Gate
  or or_2 (or_2_out, ~N3, ~N2, N1, N0);  // OR_Gate
  or or_3 (or_3_out, ~N3, ~N2, ~N1, N0);  // OR_Gate
  or or_4 (or_4_out, ~N3, ~N2, ~N1, ~N0);  // OR_Gate
  and and_1 (f_c, or_1_out, or_2_out, or_3_out, or_4_out);
endmodule

module D (
  input  N0,
  input  N1,
  input  N2,
  input  N3,
  output f_d
);

  wire or_1_out, or_2_out, or_3_out, or_4_out, or_5_out;

  or or_1 (or_1_out, N3, N2, N1, ~N0);  // OR_Gate
  or or_2 (or_2_out, N3, ~N2, N1, N0);  // OR_Gate
  or or_3 (or_3_out, N3, ~N2, ~N1, ~N0);  // OR_Gate
  or or_4 (or_4_out, ~N3, N2, ~N1, N0);  // OR_Gate
  or or_5 (or_5_out, ~N3, ~N2, ~N1, ~N0);  // OR_Gate
  and and_1 (f_d, or_1_out, or_2_out, or_3_out, or_4_out, or_5_out);
endmodule

module E (
  input  N0,
  input  N1,
  input  N2,
  input  N3,
  output f_e
);

  wire or_1_out, or_2_out, or_3_out, or_4_out, or_5_out, or_6_out;

  or or_1 (or_1_out, N3, N2, N1, ~N0);  // OR_Gate
  or or_2 (or_2_out, N3, N2, ~N1, ~N0);  // OR_Gate
  or or_3 (or_3_out, N3, ~N2, N1, N0);  // OR_Gate
  or or_4 (or_4_out, N3, ~N2, N1, ~N0);  // OR_Gate
  or or_5 (or_5_out, N3, ~N2, ~N1, ~N0);  // OR_Gate
  or or_6 (or_6_out, ~N3, N2, N1, ~N0);  // OR_Gate
  and and_1 (f_e, or_1_out, or_2_out, or_3_out, or_4_out, or_5_out, or_6_out);
endmodule

module F (
  input  N0,
  input  N1,
  input  N2,
  input  N3,
  output f_f
);

  wire or_1_out, or_2_out, or_3_out, or_4_out, or_5_out;

  or or_1 (or_1_out, N3, N2, N1, ~N0);  // OR_Gate
  or or_2 (or_2_out, N3, N2, ~N1, N0);  // OR_Gate
  or or_3 (or_3_out, N3, N2, ~N1, ~N0);  // OR_Gate
  or or_4 (or_4_out, N3, ~N2, ~N1, ~N0);  // OR_Gate
  or or_5 (or_5_out, ~N3, ~N2, N1, ~N0);  // OR_Gate
  and and_1 (f_f, or_1_out, or_2_out, or_3_out, or_4_out, or_5_out);
endmodule

module G (
  input  N0,
  input  N1,
  input  N2,
  input  N3,
  output f_g
);

  wire or_1_out, or_2_out, or_3_out, or_4_out;

  or or_1 (or_1_out, N3, N2, N1, N0);
  or or_2 (or_2_out, N3, N2, N1, ~N0);  // OR_Gate
  or or_3 (or_3_out, N3, ~N2, ~N1, ~N0);  // OR_Gate
  or or_4 (or_4_out, ~N3, ~N2, N1, N0);  // OR_Gate
  and and_1 (f_g, or_1_out, or_2_out, or_3_out, or_4_out);
endmodule

module Codificador_simple (
  input  N0,
  input  N1,
  input  N2,
  input  N3,
  input  N4,
  input  N5,
  input  N6,
  input  N7,
  input  N8,
  input  N9,
  input  NA,
  input  NB,
  input  NC,
  input  ND,
  input  NE,
  input  NF,
  output f_0,
  output f_1,
  output f_2,
  output f_3
);

  or or_1 (f_0, N0, N2, N4, N6, N8, NA, ND, NF);
  or or_2 (f_1, N1, N2, N5, N6, N9, NA, NE, NF);
  or or_3 (f_2, N3, N4, N5, N6, NC, ND, NE, NF);
  or or_4 (f_3, N8, N9, NA, NB, NC, ND, NE, NF, N7);
endmodule

module Punto_5 (
  input  in_1,
  input  in_2,
  input  in_3,
  input  in_4,
  input  in_5,
  input  in_6,
  input  in_7,
  input  in_8,
  input  in_9,
  input  in_10,
  input  in_11,
  input  in_12,
  input  in_13,
  input  in_14,
  input  in_15,
  input  in_16
);

  wire a_1_f_a, b_1_f_b, c_1_f_c, codificador_simple_1_f_0, codificador_simple_1_f_1,
       codificador_simple_1_f_2, codificador_simple_1_f_3, d_1_f_d, e_1_f_e, f_1_f_f, g_1_f_g;

  Codificador_simple codificador_simple_1 (
    .N0(in_1), .N1(in_2), .N2(in_3), .N3(in_4), .N4(in_5), .N5(in_6), .N6(in_7), .N7(in_8), .N8(in_9),
    .N9(in_10), .NA(in_11), .NB(in_12), .NC(in_13), .ND(in_14), .NE(in_15), .NF(in_16),
    .f_0(codificador_simple_1_f_0), .f_1(codificador_simple_1_f_1), .f_2(codificador_simple_1_f_2),
    .f_3(codificador_simple_1_f_3));
  F f_1 (
    .N0(codificador_simple_1_f_0), .N1(codificador_simple_1_f_1), .N2(codificador_simple_1_f_2),
    .N3(codificador_simple_1_f_3), .f_f(f_1_f_f));
  G g_1 (
    .N0(codificador_simple_1_f_0), .N1(codificador_simple_1_f_1), .N2(codificador_simple_1_f_2),
    .N3(codificador_simple_1_f_3), .f_g(g_1_f_g));
  E e_1 (
    .N0(codificador_simple_1_f_0), .N1(codificador_simple_1_f_1), .N2(codificador_simple_1_f_2),
    .N3(codificador_simple_1_f_3), .f_e(e_1_f_e));
  _7_Segment_Display u_7_segment_display_1 (
    .g(g_1_f_g), .f(f_1_f_f), .a(a_1_f_a), .b(b_1_f_b), .e(e_1_f_e), .d(d_1_f_d), .c(c_1_f_c));  // open: dp
  D d_1 (
    .N0(codificador_simple_1_f_0), .N1(codificador_simple_1_f_1), .N2(codificador_simple_1_f_2),
    .N3(codificador_simple_1_f_3), .f_d(d_1_f_d));
  A a_1 (
    .N0(codificador_simple_1_f_0), .N1(codificador_simple_1_f_1), .N2(codificador_simple_1_f_2),
    .N3(codificador_simple_1_f_3), .f_a(a_1_f_a));
  C c_1 (
    .N0(codificador_simple_1_f_0), .N1(codificador_simple_1_f_1), .N2(codificador_simple_1_f_2),
    .N3(codificador_simple_1_f_3), .f_c(c_1_f_c));
  B b_1 (
    .N0(codificador_simple_1_f_0), .N1(codificador_simple_1_f_1), .N2(codificador_simple_1_f_2),
    .N3(codificador_simple_1_f_3), .f_b(b_1_f_b));
endmodule

module Punto_6 (
  input  in_1,
  input  in_2,
  input  in_3,
  input  in_4,
  input  in_5,
  input  in_6,
  input  in_7,
  input  in_8,
  input  in_9,
  input  in_10,
  input  in_11,
  input  in_12,
  input  in_13,
  input  in_14,
  input  in_15,
  input  in_16
);

  wire a_1_f_a, and_1_out, and_2_out, and_3_out, and_4_out, and_5_out, and_6_out, and_7_out, b_1_f_b,
       c_1_f_c, codificador_simple_1_f_0, codificador_simple_1_f_1, codificador_simple_1_f_2,
       codificador_simple_1_f_3, d_1_f_d, e_1_f_e, f_1_f_f, g_1_f_g, nor_1_out;

  nor nor_1 (nor_1_out, in_1, in_2, in_3, in_4, in_5, in_6, in_7, in_8, in_9, in_10, in_11, in_12, in_13, in_14, in_15, in_16);
  Codificador_simple codificador_simple_1 (
    .N0(in_1), .N1(in_2), .N2(in_3), .N3(in_4), .N4(in_5), .N5(in_6), .N6(in_7), .N7(in_8), .N8(in_9),
    .N9(in_10), .NA(in_11), .NB(in_12), .NC(in_13), .ND(in_14), .NE(in_15), .NF(in_16),
    .f_0(codificador_simple_1_f_0), .f_1(codificador_simple_1_f_1), .f_2(codificador_simple_1_f_2),
    .f_3(codificador_simple_1_f_3));
  F f_1 (
    .N0(codificador_simple_1_f_0), .N1(codificador_simple_1_f_1), .N2(codificador_simple_1_f_2),
    .N3(codificador_simple_1_f_3), .f_f(f_1_f_f));
  and and_1 (and_1_out, f_1_f_f, ~nor_1_out);  // AND_Gate
  G g_1 (
    .N0(codificador_simple_1_f_0), .N1(codificador_simple_1_f_1), .N2(codificador_simple_1_f_2),
    .N3(codificador_simple_1_f_3), .f_g(g_1_f_g));
  and and_2 (and_2_out, g_1_f_g, ~nor_1_out);  // AND_Gate
  and and_3 (and_3_out, ~nor_1_out, e_1_f_e);  // AND_Gate
  E e_1 (
    .N0(codificador_simple_1_f_0), .N1(codificador_simple_1_f_1), .N2(codificador_simple_1_f_2),
    .N3(codificador_simple_1_f_3), .f_e(e_1_f_e));
  and and_4 (and_4_out, a_1_f_a, ~nor_1_out);  // AND_Gate
  _7_Segment_Display u_7_segment_display_1 (
    .g(and_2_out), .f(and_1_out), .a(and_4_out), .b(and_7_out), .e(and_3_out), .d(and_5_out), .c(and_6_out));  // open: dp
  and and_5 (and_5_out, ~nor_1_out, d_1_f_d);  // AND_Gate
  D d_1 (
    .N0(codificador_simple_1_f_0), .N1(codificador_simple_1_f_1), .N2(codificador_simple_1_f_2),
    .N3(codificador_simple_1_f_3), .f_d(d_1_f_d));
  and and_6 (and_6_out, c_1_f_c, ~nor_1_out);  // AND_Gate
  A a_1 (
    .N0(codificador_simple_1_f_0), .N1(codificador_simple_1_f_1), .N2(codificador_simple_1_f_2),
    .N3(codificador_simple_1_f_3), .f_a(a_1_f_a));
  and and_7 (and_7_out, b_1_f_b, ~nor_1_out);  // AND_Gate
  C c_1 (
    .N0(codificador_simple_1_f_0), .N1(codificador_simple_1_f_1), .N2(codificador_simple_1_f_2),
    .N3(codificador_simple_1_f_3), .f_c(c_1_f_c));
  B b_1 (
    .N0(codificador_simple_1_f_0), .N1(codificador_simple_1_f_1), .N2(codificador_simple_1_f_2),
    .N3(codificador_simple_1_f_3), .f_b(b_1_f_b));

  // Notes on the sheet:
  //   NADA
endmodule

module A_MUX (
  input  N3,
  input  N2,
  input  N1,
  input  N0,
  output A
);

  Multiplexer #(.select(4)) multiplexer_1 (
    .in0(1'b1), .in1(1'b0), .in2(1'b1), .in3(1'b1), .in4(1'b0), .in5(1'b1), .in6(1'b1), .in7(1'b1),
    .in8(1'b1), .in9(1'b1), .in10(1'b1), .in11(1'b0), .in12(1'b1), .in13(1'b0), .in14(1'b1), .in15(1'b1),
    .out(A), .sel({N3, N2, N1, N0}));
endmodule

module B_MUX (
  input  N3,
  input  N2,
  input  N1,
  input  N0,
  output B
);

  Multiplexer #(.select(4)) multiplexer_1 (
    .in0(1'b1), .in1(1'b1), .in2(1'b1), .in3(1'b1), .in4(1'b1), .in5(1'b0), .in6(1'b0), .in7(1'b1),
    .in8(1'b1), .in9(1'b1), .in10(1'b1), .in11(1'b0), .in12(1'b0), .in13(1'b1), .in14(1'b0), .in15(1'b0),
    .out(B), .sel({N3, N2, N1, N0}));
endmodule

module C_MUX (
  input  N3,
  input  N2,
  input  N1,
  input  N0,
  output C
);

  Multiplexer #(.select(4)) multiplexer_1 (
    .in0(1'b1), .in1(1'b1), .in2(1'b0), .in3(1'b1), .in4(1'b1), .in5(1'b1), .in6(1'b1), .in7(1'b1),
    .in8(1'b1), .in9(1'b1), .in10(1'b1), .in11(1'b1), .in12(1'b0), .in13(1'b1), .in14(1'b0), .in15(1'b0),
    .out(C), .sel({N3, N2, N1, N0}));
endmodule

module D_MUX (
  input  N3,
  input  N2,
  input  N1,
  input  N0,
  output D
);

  Multiplexer #(.select(4)) multiplexer_1 (
    .in0(1'b1), .in1(1'b0), .in2(1'b1), .in3(1'b1), .in4(1'b0), .in5(1'b1), .in6(1'b1), .in7(1'b0),
    .in8(1'b1), .in9(1'b1), .in10(1'b0), .in11(1'b1), .in12(1'b1), .in13(1'b1), .in14(1'b1), .in15(1'b0),
    .out(D), .sel({N3, N2, N1, N0}));
endmodule

module E_MUX (
  input  N3,
  input  N2,
  input  N1,
  input  N0,
  output E
);

  Multiplexer #(.select(4)) multiplexer_1 (
    .in0(1'b1), .in1(1'b0), .in2(1'b1), .in3(1'b0), .in4(1'b0), .in5(1'b0), .in6(1'b1), .in7(1'b0),
    .in8(1'b1), .in9(1'b0), .in10(1'b1), .in11(1'b1), .in12(1'b1), .in13(1'b1), .in14(1'b1), .in15(1'b1),
    .out(E), .sel({N3, N2, N1, N0}));
endmodule

module F_MUX (
  input  N3,
  input  N2,
  input  N1,
  input  N0,
  output F
);

  Multiplexer #(.select(4)) multiplexer_1 (
    .in0(1'b1), .in1(1'b0), .in2(1'b0), .in3(1'b0), .in4(1'b1), .in5(1'b1), .in6(1'b1), .in7(1'b0),
    .in8(1'b1), .in9(1'b1), .in10(1'b1), .in11(1'b1), .in12(1'b1), .in13(1'b0), .in14(1'b1), .in15(1'b1),
    .out(F), .sel({N3, N2, N1, N0}));
endmodule

module G_MUX (
  input  N3,
  input  N2,
  input  N1,
  input  N0,
  output G
);

  Multiplexer #(.select(4)) multiplexer_1 (
    .in0(1'b0), .in1(1'b0), .in2(1'b1), .in3(1'b1), .in4(1'b1), .in5(1'b1), .in6(1'b1), .in7(1'b0),
    .in8(1'b1), .in9(1'b1), .in10(1'b1), .in11(1'b1), .in12(1'b0), .in13(1'b1), .in14(1'b1), .in15(1'b1),
    .out(G), .sel({N3, N2, N1, N0}));
endmodule

module Punto_7 (
  input  N3,
  input  N2,
  input  N1,
  input  N0
);

  wire a_mux_1_a, b_mux_1_b, c_mux_1_c, d_mux_1_d, e_mux_1_e, f_mux_1_f, g_mux_1_g;

  G_MUX g_mux_1 (.N3(N3), .N2(N2), .N1(N1), .N0(N0), .G(g_mux_1_g));
  F_MUX f_mux_1 (.N3(N3), .N2(N2), .N1(N1), .N0(N0), .F(f_mux_1_f));
  E_MUX e_mux_1 (.N3(N3), .N2(N2), .N1(N1), .N0(N0), .E(e_mux_1_e));
  _7_Segment_Display u_7_segment_display_1 (
    .g(g_mux_1_g), .f(f_mux_1_f), .a(a_mux_1_a), .b(b_mux_1_b), .e(e_mux_1_e), .d(d_mux_1_d), .c(c_mux_1_c));  // open: dp
  D_MUX d_mux_1 (.N3(N3), .N2(N2), .N1(N1), .N0(N0), .D(d_mux_1_d));
  C_MUX c_mux_1 (.N3(N3), .N2(N2), .N1(N1), .N0(N0), .C(c_mux_1_c));
  A_MUX a_mux_1 (.N3(N3), .N2(N2), .N1(N1), .N0(N0), .A(a_mux_1_a));
  B_MUX b_mux_1 (.N3(N3), .N2(N2), .N1(N1), .N0(N0), .B(b_mux_1_b));
endmodule

module Punto_8 (
  input  B3,
  input  A3,
  input  B2,
  input  A2,
  input  B1,
  input  A1,
  input  B0,
  input  A0,
  output C3,
  output S3,
  output S2,
  output S1,
  output S0
);

  wire and_1_out, and_2_out, and_3_out, and_4_out, and_5_out, and_6_out, and_7_out, and_8_out, and_9_out,
       and_10_out, or_2_out, or_3_out, xor_1_out, xor_3_out, xor_5_out;

  and and_1 (and_1_out, or_2_out, B3);
  and and_2 (and_2_out, or_2_out, A3);
  or or_1 (C3, and_1_out, and_2_out, and_3_out);
  and and_3 (and_3_out, B3, A3);
  xor xor_1 (xor_1_out, B3, A3);
  xor xor_2 (S3, or_2_out, xor_1_out);
  and and_4 (and_4_out, or_3_out, B2);
  and and_5 (and_5_out, or_3_out, A2);
  or or_2 (or_2_out, and_4_out, and_5_out, and_6_out);
  and and_6 (and_6_out, B2, A2);
  xor xor_3 (xor_3_out, B2, A2);
  xor xor_4 (S2, or_3_out, xor_3_out);
  and and_7 (and_7_out, and_10_out, B1);
  and and_8 (and_8_out, and_10_out, A1);
  or or_3 (or_3_out, and_7_out, and_8_out, and_9_out);
  and and_9 (and_9_out, B1, A1);
  xor xor_5 (xor_5_out, B1, A1);
  xor xor_6 (S1, and_10_out, xor_5_out);
  and and_10 (and_10_out, B0, A0);
  xor xor_7 (S0, B0, A0);

  // Notes on the sheet:
  //   C2
  //   C1
  //   C0
endmodule

module Punto_10 (
  input  X3,
  input  X5,
  input  X6,
  input  X7,
  input  X9,
  input  X10,
  input  X11,
  input  X12,
  output P1,
  output P2,
  output P4,
  output P8
);

  wire xor_1_out, xor_2_out, xor_4_out, xor_6_out, xor_7_out, xor_8_out, xor_9_out, xor_10_out, xor_13_out,
       xor_14_out;

  xor xor_1 (xor_1_out, X9, xor_4_out);
  xor xor_2 (xor_2_out, X5, xor_1_out);
  xor xor_3 (P1, X11, xor_2_out);
  xor xor_4 (xor_4_out, X7, X3);
  xor xor_5 (P2, X3, xor_8_out);
  xor xor_6 (xor_6_out, X7, X6);
  xor xor_7 (xor_7_out, X10, xor_6_out);
  xor xor_8 (xor_8_out, X11, xor_7_out);
  xor xor_9 (xor_9_out, X7, X12);
  xor xor_10 (xor_10_out, X6, xor_9_out);
  xor xor_11 (P4, X5, xor_10_out);
  xor xor_12 (P8, X9, xor_14_out);
  xor xor_13 (xor_13_out, X11, X12);
  xor xor_14 (xor_14_out, X10, xor_13_out);
endmodule

module Punto_14 (
  input  A3,
  input  A2,
  input  A1,
  input  A0,
  output out_5,
  output out_6,
  output out_7,
  output out_8
);

  wire not_1_out, not_2_out, not_3_out, not_4_out;

  not not_1 (not_1_out, A3);
  not not_2 (not_2_out, A2);
  not not_3 (not_3_out, A1);
  not not_4 (not_4_out, A0);
  Punto_8 punto_8_1 (
    .B3(1'b0), .A3(not_1_out), .B2(1'b0), .A2(not_2_out), .B1(1'b0), .A1(not_3_out), .B0(1'b1),
    .A0(not_4_out), .S3(out_5), .S2(out_6), .S1(out_7), .S0(out_8));  // open: C3

  // Notes on the sheet:
  //   B3
  //   B2
  //   B1
  //   B0
endmodule

module Validador_paridad (
  input  P1,
  input  P2,
  input  X3,
  input  X5,
  input  P4,
  input  X6,
  input  X7,
  input  P8,
  input  X9,
  input  X10,
  input  X11,
  input  X12,
  output E1,
  output E2,
  output E4,
  output E8
);

  wire xor_1_out, xor_2_out, xor_3_out, xor_5_out, xor_6_out, xor_8_out, xor_9_out, xor_10_out, xor_12_out,
       xor_13_out, xor_14_out, xor_15_out, xor_17_out, xor_18_out;

  xor xor_1 (xor_1_out, X5, xor_5_out);
  xor xor_2 (xor_2_out, X7, xor_1_out);
  xor xor_3 (xor_3_out, X9, xor_2_out);
  xor xor_4 (E1, X11, xor_3_out);
  xor xor_5 (xor_5_out, P1, X3);
  xor xor_6 (xor_6_out, X10, xor_10_out);
  xor xor_7 (E2, X11, xor_6_out);
  xor xor_8 (xor_8_out, P2, X3);
  xor xor_9 (xor_9_out, X6, xor_8_out);
  xor xor_10 (xor_10_out, X7, xor_9_out);
  xor xor_11 (E4, X12, xor_14_out);
  xor xor_12 (xor_12_out, P4, X5);
  xor xor_13 (xor_13_out, X6, xor_12_out);
  xor xor_14 (xor_14_out, X7, xor_13_out);
  xor xor_15 (xor_15_out, X11, xor_18_out);
  xor xor_16 (E8, X12, xor_15_out);
  xor xor_17 (xor_17_out, P8, X9);
  xor xor_18 (xor_18_out, X10, xor_17_out);
endmodule

module Punto_11 (
  input  in_1,
  input  in_2,
  input  in_3,
  input  in_4,
  input  in_5,
  input  in_6,
  input  in_7,
  input  in_8,
  input  in_9,
  input  in_10,
  input  in_11,
  input  in_12
);

  wire a_1_f_a, b_1_f_b, c_1_f_c, d_1_f_d, e_1_f_e, f_1_f_f, g_1_f_g, validador_paridad_1_e1,
       validador_paridad_1_e2, validador_paridad_1_e4, validador_paridad_1_e8;

  Validador_paridad validador_paridad_1 (
    .P1(in_1), .P2(in_2), .X3(in_3), .X5(in_4), .P4(in_5), .X6(in_6), .X7(in_7), .P8(in_8), .X9(in_9),
    .X10(in_10), .X11(in_11), .X12(in_12), .E1(validador_paridad_1_e1), .E2(validador_paridad_1_e2),
    .E4(validador_paridad_1_e4), .E8(validador_paridad_1_e8));
  F f_1 (
    .N0(validador_paridad_1_e1), .N1(validador_paridad_1_e2), .N2(validador_paridad_1_e4),
    .N3(validador_paridad_1_e8), .f_f(f_1_f_f));
  G g_1 (
    .N0(validador_paridad_1_e1), .N1(validador_paridad_1_e2), .N2(validador_paridad_1_e4),
    .N3(validador_paridad_1_e8), .f_g(g_1_f_g));
  E e_1 (
    .N0(validador_paridad_1_e1), .N1(validador_paridad_1_e2), .N2(validador_paridad_1_e4),
    .N3(validador_paridad_1_e8), .f_e(e_1_f_e));
  _7_Segment_Display u_7_segment_display_1 (
    .g(g_1_f_g), .f(f_1_f_f), .a(a_1_f_a), .b(b_1_f_b), .e(e_1_f_e), .d(d_1_f_d), .c(c_1_f_c));  // open: dp
  D d_1 (
    .N0(validador_paridad_1_e1), .N1(validador_paridad_1_e2), .N2(validador_paridad_1_e4),
    .N3(validador_paridad_1_e8), .f_d(d_1_f_d));
  A a_1 (
    .N0(validador_paridad_1_e1), .N1(validador_paridad_1_e2), .N2(validador_paridad_1_e4),
    .N3(validador_paridad_1_e8), .f_a(a_1_f_a));
  C c_1 (
    .N0(validador_paridad_1_e1), .N1(validador_paridad_1_e2), .N2(validador_paridad_1_e4),
    .N3(validador_paridad_1_e8), .f_c(c_1_f_c));
  B b_1 (
    .N0(validador_paridad_1_e1), .N1(validador_paridad_1_e2), .N2(validador_paridad_1_e4),
    .N3(validador_paridad_1_e8), .f_b(b_1_f_b));
endmodule

module Half_adder (
  input  B,
  input  A,
  output C_out,
  output S
);

  and and_1 (C_out, B, A);
  xor xor_1 (S, B, A);
endmodule

module Full_adder (
  input  C_in,
  input  B,
  input  A,
  output C_out,
  output S
);

  wire and_1_out, and_2_out, and_3_out, xor_1_out;

  and and_1 (and_1_out, C_in, B);
  and and_2 (and_2_out, C_in, A);
  or or_1 (C_out, and_1_out, and_2_out, and_3_out);
  and and_3 (and_3_out, B, A);
  xor xor_1 (xor_1_out, B, A);
  xor xor_2 (S, C_in, xor_1_out);
endmodule

module Punto_8bis (
  input  B0,
  input  A0,
  input  B1,
  input  A1,
  input  B2,
  input  A2,
  input  B3,
  input  A3,
  output S0,
  output S1,
  output S2,
  output C_out,
  output S3
);

  wire full_adder_1_c_out, full_adder_2_c_out, half_adder_1_c_out;

  Half_adder half_adder_1 (.B(B0), .A(A0), .C_out(half_adder_1_c_out), .S(S0));
  Full_adder full_adder_1 (.C_in(half_adder_1_c_out), .B(B1), .A(A1), .C_out(full_adder_1_c_out), .S(S1));
  Full_adder full_adder_2 (.C_in(full_adder_1_c_out), .B(B2), .A(A2), .C_out(full_adder_2_c_out), .S(S2));
  Full_adder full_adder_3 (.C_in(full_adder_2_c_out), .B(B3), .A(A3), .C_out(C_out), .S(S3));
endmodule

module Restador_Sumador (
  input  A3,
  input  A2,
  input  A1,
  input  A0,
  input  B3,
  input  B2,
  input  B1,
  input  B0,
  input  X,
  output C_B,
  output S3,
  output S2,
  output S1,
  output S0
);

  wire full_adder_2_c_out, full_adder_3_c_out, full_adder_4_c_out, xor_1_out, xor_2_out, xor_3_out, xor_4_out;

  xor xor_1 (xor_1_out, B3, X);
  Full_adder full_adder_1 (.C_in(full_adder_2_c_out), .B(xor_1_out), .A(A3), .C_out(S3), .S(C_B));
  xor xor_2 (xor_2_out, B2, X);
  Full_adder full_adder_2 (.C_in(full_adder_3_c_out), .B(xor_2_out), .A(A2), .C_out(full_adder_2_c_out), .S(S2));
  xor xor_3 (xor_3_out, X, B1);
  Full_adder full_adder_3 (.C_in(full_adder_4_c_out), .B(xor_3_out), .A(A1), .C_out(full_adder_3_c_out), .S(S1));
  xor xor_4 (xor_4_out, X, B0);
  Full_adder full_adder_4 (.C_in(X), .B(xor_4_out), .A(A0), .C_out(full_adder_4_c_out), .S(S0));

  // Notes on the sheet:
  //   Circuito combinacional que suma o resta dos numeros binarios de 4 bits signados (con x = 0 para suma, x= 1 para resta)
endmodule
