// Logisim project Microcodigo.circ as structural Verilog
module FF_D_OE (
  input  Preset,
  input  D,
  input  CE,
  input  Clock,
  input  Reset,
  input  OE,
  output Q,
  output QOE
);

  wire and_1_out;

  D_Flip_Flop d_ff_1 (.D(D), .clk(and_1_out), .Q(Q), .preset(Preset), .reset(Reset));  // open: Qn
  and and_1 (and_1_out, CE, Clock);
  assign QOE = OE ? Q : 1'bz;  // Controlled_Buffer controlled_buffer_1
endmodule

module Latch (
  input  [3:0] D,
  input  [3:0] Preset,
  input  CE,
  input  Clock,
  input  Reset,
  input  OE,
  output [3:0] QOE,
  output [3:0] Q
);

  FF_D_OE ff_d_oe_1 (
    .Preset(Preset[3]), .D(D[3]), .CE(CE), .Clock(Clock), .Reset(Reset), .OE(OE), .Q(Q[3]), .QOE(QOE[3]));
  FF_D_OE ff_d_oe_2 (
    .Preset(Preset[2]), .D(D[2]), .CE(CE), .Clock(Clock), .Reset(Reset), .OE(OE), .Q(Q[2]), .QOE(QOE[2]));
  FF_D_OE ff_d_oe_3 (
    .Preset(Preset[1]), .D(D[1]), .CE(CE), .Clock(Clock), .Reset(Reset), .OE(OE), .Q(Q[1]), .QOE(QOE[1]));
  FF_D_OE ff_d_oe_4 (
    .Preset(Preset[0]), .D(D[0]), .CE(CE), .Clock(Clock), .Reset(Reset), .OE(OE), .Q(Q[0]), .QOE(QOE[0]));
endmodule

module Microcodigo (
  input  [3:0] in_1,
  input  in_2,
  input  [3:0] in_3,
  input  [3:0] in_4,
  input  in_5,
  input  in_6,
  input  [3:0] in_7,
  input  in_8
);

  wire clock_1_out, not_1_out;
  wire [2:0] counter_1_q;
  wire [3:0] adder_1_out, latch_1_q, latch_1_qoe, latch_2_q, latch_2_qoe, latch_3_q, latch_4_q,
       multiplexer_1_out;
  wire [7:0] rom_1_data;

  Counter #(.max('h7), .trigger("falling"), .width(3)) counter_1 (
    .Q(counter_1_q), .clk(clock_1_out));  // open: load, D, count, carry, up, clr
  ROM #(.addrWidth(3)) rom_1 (.addr(counter_1_q), .data(rom_1_data));
  Clock clock_1 (.out(clock_1_out));
  Hex_Digit_Display hex_digit_display_1 (.value(latch_1_qoe));  // open: dp
  Latch latch_1 (
    .CE(rom_1_data[3]), .Clock(clock_1_out), .Reset(in_5), .OE(rom_1_data[4]), .Preset(in_3),
    .D(latch_2_qoe), .QOE(latch_1_qoe), .Q(latch_1_q));
  not not_1 (not_1_out, rom_1_data[7]);
  Adder #(.width(4)) adder_1 (.a(latch_1_qoe), .b(latch_2_qoe), .out(adder_1_out));  // open: cin, cout
  Hex_Digit_Display #(.decimalPoint("false")) hex_digit_display_2 (.value(latch_1_q));
  Multiplexer #(.width(4)) multiplexer_1 (
    .in0(latch_1_qoe), .in1(adder_1_out), .out(multiplexer_1_out), .sel(not_1_out));
  Hex_Digit_Display hex_digit_display_3 (.value(multiplexer_1_out));  // open: dp
  Hex_Digit_Display #(.decimalPoint("false")) hex_digit_display_4 (.value(latch_2_q));
  Latch latch_2 (
    .CE(rom_1_data[5]), .Clock(clock_1_out), .Reset(in_2), .OE(rom_1_data[6]), .Preset(in_1),
    .D(multiplexer_1_out), .QOE(latch_2_qoe), .Q(latch_2_q));
  Hex_Digit_Display hex_digit_display_5 (.value(latch_2_qoe));  // open: dp
  Hex_Digit_Display #(.decimalPoint("false")) hex_digit_display_6 (.value(latch_3_q));
  Latch latch_3 (
    .CE(rom_1_data[1]), .Clock(clock_1_out), .Reset(in_6), .OE(rom_1_data[2]), .Preset(in_4),
    .D(latch_2_qoe), .QOE(latch_1_qoe), .Q(latch_3_q));
  Latch latch_4 (
    .Clock(clock_1_out), .Reset(in_8), .OE(rom_1_data[0]), .Preset(in_7), .QOE(latch_2_qoe), .Q(latch_4_q));  // open: CE, D
  Hex_Digit_Display #(.decimalPoint("false")) hex_digit_display_7 (.value(latch_4_q));

  // Notes on the sheet:
  //   contents of rom_1 (hex, n*v repeats v):
  //   11 31 42 48
  //   R0
  //   RTR
  //   R1
  //   MBR
endmodule
