// Logisim project EjemploFuncionMayoria.circ as structural Verilog
module mayoria (
  input  C,
  input  B,
  input  A,
  output F
);

  wire and_1_out, and_2_out, and_3_out, and_4_out;

  and and_1 (and_1_out, ~A, B, C);  // AND_Gate
  and and_2 (and_2_out, A, ~B, C);  // AND_Gate
  and and_3 (and_3_out, A, B, ~C);  // AND_Gate
  and and_4 (and_4_out, A, B, C);
  or or_1 (F, and_1_out, and_2_out, and_3_out, and_4_out);
endmodule
