// Logisim project FF_D_OE.circ as structural Verilog
module FF_D_OE (
  input  Preset,
  input  D,
  input  CE,
  input  Clock,
  input  Reset,
  input  OE,
  output Q,
  output QOE
);

  wire and_1_out;

  and and_1 (and_1_out, CE, Clock);
  D_Flip_Flop d_ff_1 (.D(D), .clk(and_1_out), .Q(Q), .preset(Preset), .reset(Reset));  // open: Qn
  assign QOE = OE ? Q : 1'bz;  // Controlled_Buffer controlled_buffer_1
endmodule
