// Logisim project Cableada.circ as structural Verilog
module Latch (
  input  [4:0] Preset,
  input  [4:0] D,
  input  Clock,
  input  CE,
  input  Reset,
  output [4:0] Q
);

  wire and_1_out;

  and and_1 (and_1_out, Clock, CE);
  D_Flip_Flop d_ff_1 (.D(D[0]), .clk(and_1_out), .Q(Q[0]), .preset(Preset[0]), .reset(Reset));  // open: Qn
  D_Flip_Flop d_ff_2 (.D(D[1]), .clk(and_1_out), .Q(Q[1]), .preset(Preset[1]), .reset(Reset));  // open: Qn
  D_Flip_Flop d_ff_3 (.D(D[2]), .clk(and_1_out), .Q(Q[2]), .preset(Preset[2]), .reset(Reset));  // open: Qn
  D_Flip_Flop d_ff_4 (.D(D[3]), .clk(and_1_out), .Q(Q[3]), .preset(Preset[3]), .reset(Reset));  // open: Qn
  D_Flip_Flop d_ff_5 (.D(D[4]), .clk(and_1_out), .Q(Q[4]), .preset(Preset[4]), .reset(Reset));  // open: Qn
endmodule

module Cableada (
  input  [4:0] in_1,
  input  in_2,
  input  [4:0] in_3,
  input  in_4,
  input  [4:0] in_5,
  input  in_6,
  input  [4:0] in_7,
  input  in_8
);

  wire bussplit_1_bitf, bussplit_2_bitf, bussplit_3_bitf, bussplit_4_bitf, bussplit_5_bitf, bussplit_6_bitf,
       clock_1_out, demultiplexer_1_out0, demultiplexer_1_out1, demultiplexer_1_out2, demultiplexer_1_out3;
  wire [1:0] rom_1_data, rom_1_data_3, rom_1_data_4;
  wire [2:0] counter_1_q;
  wire [3:0] bussplit_1_hexout, bussplit_2_hexout, bussplit_3_hexout, bussplit_4_hexout, bussplit_5_hexout,
       bussplit_6_hexout;
  wire [4:0] adder_1_out, latch_1_q, latch_2_q, latch_3_q, latch_4_q, multiplexer_1_out, multiplexer_2_out,
       multiplexer_3_out, multiplexer_4_out, subtractor_1_out;
  wire [7:6] rom_1_data_2;

  Demultiplexer #(.select(2)) demultiplexer_1 (
    .out0(demultiplexer_1_out0), .out1(demultiplexer_1_out1), .out2(demultiplexer_1_out2),
    .out3(demultiplexer_1_out3), .in(1'b1), .sel(rom_1_data));
  Clock clock_1 (.out(clock_1_out));
  Counter #(.max('h7), .trigger("falling"), .width(3)) counter_1 (
    .Q(counter_1_q), .clk(clock_1_out));  // open: load, D, count, carry, up, clr
  ROM #(.addrWidth(3)) rom_1 (.addr(counter_1_q), .data({rom_1_data_2, rom_1_data, rom_1_data_4, rom_1_data_3}));
  _7_Segment_Display #(.decimalPoint("false")) u_7_segment_display_1 (
    .b(bussplit_1_bitf), .c(bussplit_1_bitf));  // open: g, f, a, e, d
  Latch latch_1 (
    .Clock(clock_1_out), .CE(demultiplexer_1_out0), .D(multiplexer_4_out), .Preset(in_1), .Reset(in_2),
    .Q(latch_1_q));
  _7_Segment_Display #(.decimalPoint("false")) u_7_segment_display_2 (
    .b(bussplit_2_bitf), .c(bussplit_2_bitf));  // open: g, f, a, e, d
  Latch latch_2 (
    .Clock(clock_1_out), .CE(demultiplexer_1_out1), .D(multiplexer_4_out), .Preset(in_3), .Reset(in_4),
    .Q(latch_2_q));
  _7_Segment_Display #(.decimalPoint("false")) u_7_segment_display_3 (
    .b(bussplit_3_bitf), .c(bussplit_3_bitf));  // open: g, f, a, e, d
  Latch latch_3 (
    .Clock(clock_1_out), .CE(demultiplexer_1_out2), .D(multiplexer_4_out), .Preset(in_5), .Reset(in_6),
    .Q(latch_3_q));
  _7_Segment_Display #(.decimalPoint("false")) u_7_segment_display_4 (
    .b(bussplit_4_bitf), .c(bussplit_4_bitf));  // open: g, f, a, e, d
  Latch latch_4 (
    .Clock(clock_1_out), .CE(demultiplexer_1_out3), .D(multiplexer_4_out), .Preset(in_7), .Reset(in_8),
    .Q(latch_4_q));
  Hex_Digit_Display #(.decimalPoint("false")) hex_digit_display_1 (.value(bussplit_1_hexout));
  BusSplit bussplit_1 (.DataIn(latch_1_q), .HexOut(bussplit_1_hexout), .bitF(bussplit_1_bitf));
  Hex_Digit_Display #(.decimalPoint("false")) hex_digit_display_2 (.value(bussplit_2_hexout));
  BusSplit bussplit_2 (.DataIn(latch_2_q), .HexOut(bussplit_2_hexout), .bitF(bussplit_2_bitf));
  Hex_Digit_Display #(.decimalPoint("false")) hex_digit_display_3 (.value(bussplit_3_hexout));
  BusSplit bussplit_3 (.DataIn(latch_3_q), .HexOut(bussplit_3_hexout), .bitF(bussplit_3_bitf));
  Hex_Digit_Display #(.decimalPoint("false")) hex_digit_display_4 (.value(bussplit_4_hexout));
  BusSplit bussplit_4 (.DataIn(latch_4_q), .HexOut(bussplit_4_hexout), .bitF(bussplit_4_bitf));
  Multiplexer #(.select(2), .width(5)) multiplexer_1 (
    .in0(latch_1_q), .in1(latch_2_q), .in2(latch_3_q), .in3(latch_4_q), .out(multiplexer_1_out),
    .sel(rom_1_data_4));
  Multiplexer #(.select(2), .width(5)) multiplexer_2 (
    .in0(latch_1_q), .in1(latch_2_q), .in2(latch_3_q), .in3(latch_4_q), .out(multiplexer_2_out),
    .sel(rom_1_data_3));
  Adder #(.width(5)) adder_1 (.a(multiplexer_1_out), .b(multiplexer_2_out), .out(adder_1_out));  // open: cin, cout
  Subtractor #(.width(5)) subtractor_1 (
    .a(multiplexer_1_out), .b(multiplexer_2_out), .out(subtractor_1_out));  // open: bin, bout
  _7_Segment_Display #(.decimalPoint("false")) u_7_segment_display_5 (
    .b(bussplit_5_bitf), .c(bussplit_5_bitf));  // open: g, f, a, e, d
  Multiplexer #(.width(5)) multiplexer_3 (
    .in0(adder_1_out), .in1(subtractor_1_out), .out(multiplexer_3_out), .sel(rom_1_data_2[6]));
  Hex_Digit_Display #(.decimalPoint("false")) hex_digit_display_5 (.value(bussplit_5_hexout));
  BusSplit bussplit_5 (.DataIn(multiplexer_3_out), .HexOut(bussplit_5_hexout), .bitF(bussplit_5_bitf));
  Multiplexer #(.width(5)) multiplexer_4 (
    .in0(multiplexer_3_out), .in1({rom_1_data_2[6], rom_1_data_4, rom_1_data_3}), .out(multiplexer_4_out),
    .sel(rom_1_data_2[7]));
  _7_Segment_Display #(.decimalPoint("false")) u_7_segment_display_6 (
    .b(bussplit_6_bitf), .c(bussplit_6_bitf));  // open: g, f, a, e, d
  Hex_Digit_Display #(.decimalPoint("false")) hex_digit_display_6 (.value(bussplit_6_hexout));
  BusSplit bussplit_6 (.DataIn(multiplexer_4_out), .HexOut(bussplit_6_hexout), .bitF(bussplit_6_bitf));

  // Notes on the sheet:
  //   contents of rom_1 (hex, n*v repeats v):
  //   4e
endmodule

module BusSplit (
  input  [4:0] DataIn,
  output [3:0] HexOut,
  output bitF
);


  assign bitF = DataIn[4];
  assign HexOut = DataIn[3:0];
endmodule
